# Fritzing sketch reator (saved by Fritzing 0.9.3b)
circuit board: 6cm x 6cm
breadboards: 1

parts:
  R2 = Resistor [tolerance=±5% resistance=330 package=THT]
  J2 = Terminal Block - 3 pins [package=THT]
  U2 = WS2812 RGB LED strip  # not connected
  U1 = WS2812 RGB LED strip
  S2 = Pushbutton [package="[THT]"]
  R1 = Resistor [tolerance=±5% resistance=330 package=THT]
  TRM1 = Terminal 2pin
  S1 = Pushbutton [package="[THT]"]
  Componente1 = Arduino Nano (Rev3.0)
  J3 = Terminal Block - 3 pins [package=THT]

nets:
  N1: R2.Pin_0, Componente1.D8
  N2: R2.Pin_1, J3.Line_2
  VCC: J2.Line_1, U1.VCC, TRM1.pin_2, Componente1.VIN, J3.Line_1
  N3: J2.Line_2, U1.DIN, R1.Pin_1
  N4: S2.Pin_1, S2.Pin_2, TRM1.pin_1, S1.Pin_1, S1.Pin_2
  N5: S2.Pin_3, S2.Pin_4, Componente1.D3
  N6: R1.Pin_0, Componente1.D7
  N7: S1.Pin_3, S1.Pin_4, Componente1.D2

custom parts:
  Terminal Block - 3 pins: Generic Screw Terminal 8mm
  WS2812 RGB LED strip: WS2812 strip
  Terminal 2pin: 2-pin Terminal Block
